// Logisim project RISC16_Saje.circ as structural Verilog: 4 circuits, main circuit main
module main (
);

  wire clock_1_out;
  wire [3:0] rom_1_data, rom_1_data_2;
  wire [7:0] rom_1_data_3;
  wire [15:0] pc_1_o;

  Clock clock_1 (.out(clock_1_out));
  PC pc_1 (.EN(clock_1_out), .CLK(clock_1_out), .O(pc_1_o));  // open: JMP_ADDR, JMP_EN
  ROM #(.addrWidth(16), .dataWidth(16)) rom_1 (.addr(pc_1_o), .data({rom_1_data_3, rom_1_data_2, rom_1_data}));
endmodule

module OneTickLatch (
  input  CLK,
  output out_2
);

  wire not_1_out, register_1_q;

  Register #(.width(1)) register_1 (.D(1'b1), .clk(CLK), .Q(register_1_q));  // open: en, clr
  not not_1 (not_1_out, register_1_q);
  and and_1 (out_2, not_1_out, CLK);
endmodule

module PC (
  input  [15:0] JMP_ADDR,
  input  JMP_EN,
  input  EN,
  input  CLK,
  output [15:0] O
);

  wire oneticklatch_1_out_2;
  wire [15:0] adder_1_out, multiplexer_1_out;

  Adder #(.width(16)) adder_1 (.a(O), .b(16'h1), .out(adder_1_out));  // open: cin, cout
  Register #(.width(16)) register_1 (.D(multiplexer_1_out), .en(EN), .clk(CLK), .Q(O), .clr(oneticklatch_1_out_2));
  Multiplexer #(.width(16)) multiplexer_1 (.in0(adder_1_out), .in1(JMP_ADDR), .out(multiplexer_1_out), .sel(JMP_EN));
  OneTickLatch oneticklatch_1 (.CLK(CLK), .out_2(oneticklatch_1_out_2));
endmodule

module Test (
  input  in_1,
  input  in_2,
  output out_3
);

  wire not_1_out, not_2_out;

  not not_1 (not_1_out, in_1);
  not not_2 (not_2_out, in_2);
  nand nand_1 (out_3, not_1_out, not_2_out);
endmodule
